# Fritzing sketch perfboard (saved by Fritzing 0.9.3b)
stripboards: 2

parts:
  Q2 = Basic FET N-Channel [package="D2Pak [SMD]"]  # not connected
  J1 = Camdenboss CTB0158-2 [part_number=CTB0158-2 package=THT]  # not connected
  U3 = atmega328 [package=dip]
  Y3 = Resonator [frequency="16 Mhz" package=THT]
  S4 = Momentary Switch [package=ksa_sealed_tac_switch]
  R16 = Resistor [tolerance=±5% resistance=10k package=THT]  # not connected
  R17 = Resistor [tolerance=±5% resistance=10k package=THT]  # not connected
  R18 = Resistor [tolerance=±5% resistance=10k package=THT]
  R19 = Resistor [tolerance=±5% resistance=10k package=THT]
  JP3 = Header 3 [package=molex-1x3_lock]
  Display = female pin header, 4 pins [form="♀ (female)"]
  Poti = female pin header, 3 pins [form="♀ (female)"]
  J9 = female pin header, 6 pins [form="♀ (female)"]
  Therm = female pin header, 5 pins [form="♀ (female)"]
  R20 = Resistor [tolerance=±5% resistance=10k package=THT]
  C6 = Ceramic Capacitor [capacitance="100 nF" package="1206 [SMD, multilayer]"]
  U4 = atmega328 [package=dip]
  Y4 = Resonator [frequency="16 Mhz" package=THT]
  S5 = Momentary Switch [package=ksa_sealed_tac_switch]
  R21 = Resistor [tolerance=±5% resistance=10k package=THT]
  R22 = Resistor [tolerance=±5% resistance=10k package=THT]
  R23 = Resistor [tolerance=±5% resistance=10k package=THT]
  R24 = Resistor [tolerance=±5% resistance=10k package=THT]
  R25 = Resistor [tolerance=±5% resistance=10k package=THT]
  JP4 = Header 3 [package=molex-1x3_lock]
  J11 = female pin header, 3 pins [form="♀ (female)"]
  J12 = female pin header, 5 pins [form="♀ (female)"]
  J13 = female pin header, 4 pins [form="♀ (female)"]
  J14 = female pin header, 6 pins [form="♀ (female)"]
  C7 = Ceramic Capacitor [capacitance="100 nF" package="1206 [SMD, multilayer]"]
  EXT = female pin header, 3 pins [form="♀ (female)"]

nets:
  N1: U3.RESET, S4.2, R20.Pin_1, C6.1
  N2: U3.D0_(RX), J9.pin4
  N3: U3.D1_(TX), J9.pin5
  N4: U3.GND#7, U3.XLAT1, U3.XLAT2, Y3.0, Y3.GND, Y3.pin_1
  N5: U3.AVCC, U3.AREF, EXT.pin2
  N6: U3.GND#21, Poti.pin1, EXT.pin3
  N7: U3.A2, EXT.pin1
  N8: U3.A3, Poti.pin2
  N9: U3.A4, Display.pin3, Therm.pin2
  N10: U3.A5, Display.pin4, Therm.pin3
  N11: R18.Pin_0, R19.Pin_0, JP3.1, JP3.2
  N12: Display.pin2, Poti.pin3, Therm.pin1
  N13: J9.pin6, C6.0
  N14: Therm.pin4, Therm.pin5
  N15: U4.RESET, S5.2, R23.Pin_1, C7.1
  N16: U4.D0_(RX), J14.pin4
  N17: U4.D1_(TX), J14.pin5
  N18: U4.XLAT1, U4.XLAT2, Y4.0, Y4.GND, Y4.pin_1
  N19: U4.D9_(PWM), R24.Pin_1
  N20: U4.D10_(PWM), R21.Pin_1
  N21: U4.AVCC, U4.AREF
  N22: U4.A3, J11.pin2
  N23: U4.A4, J12.pin2, J13.pin3
  N24: R22.Pin_0, R25.Pin_0, JP4.1, JP4.2
  N25: J11.pin3, J12.pin1, J13.pin2
  N26: J12.pin3, J13.pin4
  N27: J14.pin6, C7.0
